# Fritzing sketch brewbuild_test_platform (saved by Fritzing 0.9.3b)
breadboards: 1

parts:
  Raspberry_Pi_1 = Raspberry Pi 3 [part_number=RPI-3-V1.2]
  IC1 = MCP3008 8-channel 10-bit ADC [part_number=MCP3008]
  IC2 = IC, DIP package, 14 pins [chip_label=MCP4922]

nets:
  N1: Raspberry_Pi_1.3v3, IC1.no_name_yet#15, IC1.no_name_yet#16, IC2.pin8, IC2.pin9, IC2.pin12
  N2: Raspberry_Pi_1.GIPO10, IC1.no_name_yet#11, IC2.pin5
  N3: Raspberry_Pi_1.GIPO9, IC1.no_name_yet#12
  N4: Raspberry_Pi_1.GIPO11, IC1.no_name_yet#13, IC2.pin4
  N5: Raspberry_Pi_1.GND, IC1.no_name_yet#9, IC1.no_name_yet#14, IC2.pin11, IC2.pin13
  N6: Raspberry_Pi_1.GIPO12, IC2.pin3
  N7: Raspberry_Pi_1.GIPO8, IC1.no_name_yet#10
  N8: Raspberry_Pi_1.GIPO18, IC1.no_name_yet#1
  N9: IC1.no_name_yet#2, IC2.pin14

notes:
  MCP3008/MCP4922 RPi 3 Test Platform
  ----------------------------------------
  ADC:
  Yellow: 3k8 13 <-> GPIO11 (SCLK)
  White: 3k8 12 <-> GPIO9 (MISO)
  Orange: 3k8 11 <-> GPIO10 (MOSI)
  Purple: 3k8 10 <-> GPIO8 (CE0)
  Pink: 3k8 A0 <-> GPIO18 (PWM)
  DAC:
  Green: DAC (LDAC 8) <-> Gnd
  Brown: DAC(In0) <-> ADC A1
  Lt. Blue (DAC CS 3) <-> GPIO 12
  Yellow (DAC SCK 4) <-> Pi SCLK
  Orange (DAC SDI 5) <-> Pi MOSI
